# Fritzing sketch seatmotion_alpha (saved by Fritzing 0.9.3b)
breadboards: 1

parts:
  M1 = DOIT Esp32 DevKit v1 (30 pins long, 11 pins width) [part_number=ESP32S-PIN30]
  R1 = Resistor [tolerance=±5% resistance=220 package=THT]
  J1 = Basic Force Sensing Resistor (FSR) [package=THT]

nets:
  N1: M1.GND, J1.pin_1
  N2: M1.D14, R1.Pin_1, J1.pin_0
  N3: M1.VIN, R1.Pin_0

custom parts:
  DOIT Esp32 DevKit v1 (30 pins long, 11 pins width): The DOIT Esp32 DevKit v1 is one of the development board created by DOIT to evaluate the ESP-WROOM-32 module. It is based on the ESP32 microcontroller that boasts Wifi, Bluetooth, Ethernet and Low Power support all in a single chip. (vanepp) made breadboard work, adjusted pin numbering and labels and reduced size of schematic and cleaned up pcb. This chip is 30pins long (2 x15) and 11 pins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
